# Fritzing sketch Drawing (saved by Fritzing 0.9.3b)
breadboards: 1

parts:
  Part1 = Arduino Mega ADK (Rev3)
  Part2 = Triple Axis Accelerometer Breakout - ADXL335
  hc-sr1 = hc-sr04
  hc-sr2 = hc-sr04
  hc-sr3 = hc-sr04
  hc-sr4 = hc-sr04
  Part3 = Bluetooth HC-05 Macho
  R1 = Resistor [tolerance=±1% resistance=510 package=THT]
  R2 = Resistor [tolerance=±1% resistance=510 package=THT]
  R3 = Resistor [tolerance=±5% resistance=150 package=THT]
  R4 = Resistor [tolerance=±5% resistance=150 package=THT]
  R5 = Resistor [tolerance=±5% resistance=150 package=THT]
  R6 = Resistor [tolerance=±5% resistance=150 package=THT]
  LED2 = LED - 5mm [color="Red (633nm)" package="5 mm [THT]"]
  LED3 = LED - 5mm [color="Red (633nm)" package="5 mm [THT]"]
  LED4 = smd LED [color="White (8000K)" package="0805 [SMD]"]
  LED5 = smd LED [color="White (8000K)" package="0805 [SMD]"]
  R7 = Resistor [tolerance=±5% resistance=22k package=THT]
  R8 = Resistor [tolerance=±5% resistance=10k package=THT]
  R10 = Photocell (LDR) [package=THT]
  R11 = Temperature Sensor (Thermistor) [thermistor_type=NTC package=THT]
  J1 = Piezo Speaker
  R12 = Resistor [tolerance=±5% resistance=150 package=THT]

nets:
  VCC: Part1.A0, Part1.5V, hc-sr1.VCC, hc-sr2.VCC, Part3.VCC, R11.pin_0
  N1: Part1.A1, R8.Pin_1, R10.pin_1
  N2: Part1.A2, Part2.ZOUT
  N3: Part1.A3, Part2.YOUT
  N4: Part1.A4, Part2.XOUT
  N5: Part1.D12_PWM, hc-sr1.Trig
  N6: Part1.D11_PWM, hc-sr1.Echo
  N7: Part1.D10_PWM, hc-sr4.Trig
  N8: Part1.D9_PWM, hc-sr4.Echo
  N9: Part1.D8_PWM, hc-sr3.Trig
  3V3: Part1.3V3, Part2.VCC
  GND: Part1.GND, Part2.GND, hc-sr1.GND, hc-sr2.GND, Part3.GND, R2.Pin_0, LED2.anode, LED3.anode, LED4.anode, LED5.anode, R7.Pin_0, R8.Pin_0, R10.pin_0, R12.Pin_0
  N10: Part1.D3_PWM, J1.pin2
  N11: Part1.D5_PWM, hc-sr2.Echo
  N12: Part1.D6_PWM, hc-sr2.Trig
  N13: Part1.D7_PWM, hc-sr3.Echo
  N14: Part1.D44, R5.Pin_0
  N15: Part1.D45, R6.Pin_0
  N16: Part1.D46, R4.Pin_0
  N17: Part1.D47, R3.Pin_0
  N18: Part1.D48, Part3.TXD
  N19: Part1.D49, R1.Pin_0
  N20: Part3.RXD, R1.Pin_1, R2.Pin_1
  N21: R3.Pin_1, LED5.cathode
  N22: R4.Pin_1, LED4.cathode
  N23: R5.Pin_1, LED3.cathode
  N24: R6.Pin_1, LED2.cathode
  N25: R7.Pin_1, R11.pin_1
  N26: J1.pin1, R12.Pin_1
